# Fritzing sketch WemosSantaHat (saved by Fritzing 0.9.4)
breadboards: 1

parts:
  WeMos_D1_Mini1 = WeMos D1 Mini
  NEOPIXEL1 = Neopixel Strip -- Black (60/m) [part_number=1461]
  LED2 = prefix0000
  WeMos_D1_Mini_Battery_Shield1 = WeMos D1 Mini Battery Shield  # not connected
  U1 = LIPO-110mAh [package=lipo-110]  # not connected

nets:
  N1: WeMos_D1_Mini1.5V, NEOPIXEL1.+5V#1
  N2: WeMos_D1_Mini1.D5, LED2.connector2
  N3: WeMos_D1_Mini1.D8, NEOPIXEL1.DI
  N4: WeMos_D1_Mini1.G, NEOPIXEL1.GND#3
  N5: NEOPIXEL1.GND#4, LED2.connector3
  N6: NEOPIXEL1.+5V#6, LED2.connector1

notes:
  Note: You should add a Capazitaor and a Resistor see best practise : https://learn.adafruit.com/adafruit-neopixel-uberguide/best-practices
  Singel NeoPixel or a 5mm Diffused one
  Battery .. I used 750mAh
  Battery Charger Hat

custom parts:
  Neopixel Strip -- Black (60/m): Neopixel Strip, Black, 60 pixels per meter.
