# Fritzing sketch markus sanda hat (saved by Fritzing 0.9.4)

parts:
  Part1 = Arduino Nano (Rev3.0)
  Part2 = Power Cell LiPo Charger/Booster
  BAT1 = Battery Holders [package=lipo-1100mAh]
  Bauteil5 = NeoPixel Stick [part_number=1426]
  LED1 = DUO LED RG [package="5 mm [THT]"]

nets:
  GND: Part1.GND, Part2.GND, BAT1.-
  N1: Part1.D11/MOSI, LED1.common_cathode
  N2: Part1.D12/MISO, Bauteil5.DATAIN
  VIN: Part1.VIN, Part2.VCC
  5V: Part1.5V, Bauteil5.+5V
  N3: Bauteil5.GND, LED1.green_anode

notes:
  This is a singel difused neopixel ...please check the wiring ...i used a led for ilustration
  this is a battery charger and pooster there are lots of potions ... orginality i just used a booster

custom parts:
  NeoPixel Stick: Make your own little LED strip arrangement with this stick of NeoPixel LEDs. We crammed 8 of the tiny 5050 (5mm x 5mm) smart RGB LEDs onto a PCB with mounting holes and a chainable design. Use only one microcontroller pin to control as many as you can chain together! Each LED is addressable as the driver chip is inside the LED. Each one has ~18mA constant current drive so the color will be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
